// Logisim project alu.circ as structural Verilog
module ALU (
  input  Clock,
  input  [31:0] Operand_1,
  input  [31:0] Operand_2,
  input  [4:0] ShfAmt,
  input  [3:0] ALUOp,
  output [31:0] ALUResult,
  output Zero,
  output Less_than_zero,
  output Greater_than_zero
);

  wire comparator_1_lt;
  wire [31:0] adder_1_out, and_1_out, bit_extender_1_out, bit_extender_2_out, bit_extender_3_out,
       bit_extender_4_out, nor_1_out, or_1_out, shifter_1_out, shifter_2_out, shifter_3_out,
       subtractor_1_out, subtractor_2_out, undriven, undriven_2, undriven_3, xor_1_out;

  Comparator #(.width(32)) comparator_1 (.a(Operand_1), .b(Operand_2), .lt(comparator_1_lt));  // open: gt, eq
  Shifter #(.width(32)) shifter_1 (.in(Operand_1), .\dist (ShfAmt), .out(shifter_1_out));
  Bit_Extender #(.in_width(32), .out_width(32), .\type ("sign")) bit_extender_1 (
    .in(Operand_1), .out(bit_extender_1_out));
  Bit_Extender #(.in_width(32), .out_width(32), .\type ("sign")) bit_extender_2 (
    .in(Operand_2), .out(bit_extender_2_out));
  Adder #(.width(32)) adder_1 (.a(Operand_1), .b(Operand_2), .out(adder_1_out));  // open: cin, cout
  Subtractor #(.width(32)) subtractor_1 (.a(Operand_1), .b(Operand_2), .out(subtractor_1_out));  // open: bin, bout
  assign and_1_out = Operand_1 & Operand_2;  // AND_Gate and_1, 32 bits wide
  assign or_1_out = Operand_1 | Operand_2;  // OR_Gate or_1, 32 bits wide
  assign xor_1_out = Operand_1 ^ Operand_2;  // XOR_Gate xor_1, 32 bits wide
  assign nor_1_out = ~(Operand_1 | Operand_2);  // NOR_Gate nor_1, 32 bits wide
  Shifter #(.width(32), .shift("lr")) shifter_2 (.in(Operand_1), .\dist (ShfAmt), .out(shifter_2_out));
  Shifter #(.width(32), .shift("ar")) shifter_3 (.in(Operand_1), .\dist (ShfAmt), .out(shifter_3_out));
  Adder #(.width(32)) adder_2 (.a(bit_extender_1_out), .b(bit_extender_2_out), .out(adder_1_out));  // open: cin, cout
  Subtractor #(.width(32)) subtractor_2 (
    .a(bit_extender_1_out), .b(bit_extender_2_out), .out(subtractor_2_out));  // open: bin, bout
  assign bit_extender_3_out = {{31{1'b0}}, comparator_1_lt};  // Bit_Extender bit_extender_3
  Bit_Extender #(.in_width(32), .out_width(32), .\type ("sign")) bit_extender_4 (
    .in(bit_extender_3_out), .out(bit_extender_4_out));
  Comparator #(.width(32)) comparator_2 (
    .a(bit_extender_3_out), .b({32{1'b0}}), .gt(Less_than_zero), .eq(Zero), .lt(Greater_than_zero));
  Multiplexer #(.select(4), .width(32), .enable("false")) multiplexer_1 (
    .in0(adder_1_out), .in1(adder_1_out), .in2(subtractor_2_out), .in3(subtractor_1_out), .in4(and_1_out),
    .in5(or_1_out), .in6(xor_1_out), .in7(nor_1_out), .in8(undriven), .in9(undriven_2),
    .in10(bit_extender_4_out), .in11(bit_extender_3_out), .in12(shifter_1_out), .in13(undriven_3),
    .in14(shifter_2_out), .in15(shifter_3_out), .out(ALUResult), .sel(ALUOp));

  // Notes on the sheet:
  //   Entradas
  //   Control
  //   Salidas
endmodule
