// Logisim project logic_gates.circ as structural Verilog
module AND (
  input  A,
  input  B,
  output R
);

  wire and_1_out, transistor_1_out;

  Transistor #(.\type ("n")) transistor_1 (.in(1'b1), .out(transistor_1_out), .gate(A));
  Transistor #(.\type ("n")) transistor_2 (.in(transistor_1_out), .out(R), .gate(B));
  Transistor #(.gate("br")) transistor_3 (.in(1'b0), .out(R), .gate(B));
  Transistor transistor_4 (.in(1'b0), .out(R), .gate(A));
  and and_1 (and_1_out, A, B);
  // Probe on and_1_out

  // Notes on the sheet:
  //   B: pull=down
  //   A: pull=down
  //   Pull Up Network
  //   x
  //   x
  //   R = A x B
  //   Pull Down Network
endmodule

module NAND (
  input  A,
  input  B,
  output X
);

  wire nand_1_out, R, transistor_3_out;

  Transistor transistor_1 (.in(1'b1), .out(R), .gate(A));
  Transistor #(.\type ("n")) transistor_2 (.in(transistor_3_out), .out(R), .gate(A));
  Transistor #(.\type ("n")) transistor_3 (.in(1'b0), .out(transistor_3_out), .gate(B));
  // Probe on nand_1_out
  nand nand_1 (nand_1_out, A, B);
  Transistor #(.gate("br")) transistor_4 (.in(1'b1), .out(R), .gate(B));

  // Notes on the sheet:
  //   A: pull=down
  //   Pull Up Network
  //   x
  //   x
  //   Pull Down Network
endmodule

module NOR (
  input  A,
  input  B,
  output X
);

  wire nor_1_out, R, transistor_1_out;

  Transistor transistor_1 (.in(1'b1), .out(transistor_1_out), .gate(A));
  Transistor transistor_2 (.in(transistor_1_out), .out(R), .gate(B));
  Transistor #(.\type ("n"), .gate("br")) transistor_3 (.in(1'b0), .out(R), .gate(B));
  Transistor #(.\type ("n")) transistor_4 (.in(1'b0), .out(R), .gate(A));
  nor nor_1 (nor_1_out, A, B);
  // Probe on nor_1_out

  // Notes on the sheet:
  //   B: pull=down
  //   A: pull=down
  //   Pull Up Network
  //   x
  //   x
endmodule

module NOT (
  input  A,
  output X
);

  wire not_1_out, R;

  Transistor transistor_1 (.in(1'b1), .out(R), .gate(A));
  Transistor #(.\type ("n")) transistor_2 (.in(1'b0), .out(R), .gate(A));
  not not_1 (not_1_out, A);
  // Probe on not_1_out

  // Notes on the sheet:
  //   A: pull=down
  //   Pull Up Network
  //   x
  //   x
endmodule

module OR (
  input  A,
  input  B,
  output X
);

  wire or_1_out, R, transistor_4_out;

  Transistor #(.\type ("n"), .gate("br")) transistor_1 (.in(1'b1), .out(R), .gate(B));
  Transistor #(.\type ("n")) transistor_2 (.in(1'b1), .out(R), .gate(A));
  Transistor transistor_3 (.in(transistor_4_out), .out(R), .gate(A));
  Transistor transistor_4 (.in(1'b0), .out(transistor_4_out), .gate(B));
  or or_1 (or_1_out, A, B);
  // Probe on or_1_out

  // Notes on the sheet:
  //   A: pull=down
  //   Pull Up Network
  //   x
  //   x
  //   Pull Down Network
  //   X = A + B
endmodule

module RS (
  input  R,
  input  S,
  output Qx,
  output Qx_prime
);

  wire and_1_r, and_2_r, clock_1_out;

  Clock clock_1 (.out(clock_1_out));
  AND and_1 (.A(R), .B(clock_1_out), .R(and_1_r));
  AND and_2 (.A(clock_1_out), .B(S), .R(and_2_r));
  NOR nor_1 (.A(and_1_r), .B(Qx_prime), .X(Qx));
  NOR nor_2 (.A(Qx), .B(and_2_r), .X(Qx_prime));
endmodule

module XOR (
  input  A,
  input  B,
  output X
);

  wire not_1_out, not_2_out, not_3_out, not_4_out, R, transistor_1_out, transistor_3_out, transistor_7_out,
       transistor_8_out, xor_1_out;

  not not_1 (not_1_out, A);
  Transistor #(.gate("br")) transistor_1 (.in(transistor_3_out), .out(transistor_1_out), .gate(B));
  Transistor transistor_2 (.in(transistor_3_out), .out(transistor_1_out), .gate(A));
  Transistor transistor_3 (.in(R), .out(transistor_3_out), .gate(not_1_out));
  Transistor #(.gate("br")) transistor_4 (.in(R), .out(transistor_3_out), .gate(not_2_out));
  not not_2 (not_2_out, B);
  Transistor #(.\type ("n"), .gate("br")) transistor_5 (.in(transistor_8_out), .out(R), .gate(not_3_out));
  Transistor #(.\type ("n")) transistor_6 (.in(transistor_7_out), .out(R), .gate(A));
  not not_3 (not_3_out, A);
  Transistor #(.\type ("n")) transistor_7 (.in(1'b0), .out(transistor_7_out), .gate(B));
  Transistor #(.\type ("n"), .gate("br")) transistor_8 (.in(1'b0), .out(transistor_8_out), .gate(not_4_out));
  not not_4 (not_4_out, B);
  xor xor_1 (xor_1_out, A, B);
  // Probe on xor_1_out
  // also tied to VCC on the sheet: transistor_1_out

  // Notes on the sheet:
  //   A: pull=down
  //   Pull Up Network
  //   x
  //   x
  //   Pull Down Network
  //   X = A'B + AB'
  //   x
endmodule

module XNOR (
  input  A,
  input  B,
  output X
);

  wire xnor_1_out;

  // Probe on xnor_1_out
  xnor xnor_1 (xnor_1_out, A, B);

  // Notes on the sheet:
  //   A: pull=down
  //   X = AB + A'B'
endmodule

module Full_Adder (
  input  A,
  input  B,
  input  C,
  output S,
  output Carry
);


  // Notes on the sheet:
  //   B: pull=down
  //   C: pull=down
  //   A: pull=down
endmodule
