// Logisim project register_file.circ as structural Verilog: 1 circuit, main circuit Register File
module Register_File (
  input  Clock,
  input  [4:0] rs,
  input  [4:0] rt,
  input  [4:0] Write_register,
  input  [31:0] Write_data,
  input  RegWrite,
  output [31:0] d1,
  output [31:0] d2
);

  wire undriven_4, undriven_5, undriven_6, undriven_8, undriven_12, undriven_13, undriven_14, undriven_16,
       undriven_20, undriven_21, undriven_22, undriven_27, undriven_28, undriven_29, undriven_30,
       undriven_35, undriven_36, undriven_37, undriven_38, undriven_43, undriven_44, undriven_45,
       undriven_46, undriven_51, undriven_52, undriven_53, undriven_54, undriven_59, undriven_60,
       undriven_61, undriven_62;
  wire [31:0] multiplexer_1_out, multiplexer_2_out, multiplexer_3_out, multiplexer_4_out, multiplexer_5_out,
       multiplexer_6_out, multiplexer_7_out, multiplexer_8_out, R1_q, R2_q, R3_q, R4_q, R5_q, R6_q, R7_q,
       R8_q, R9_q, R10_q, R11_q, R12_q, R13_q, R14_q, R15_q, R16_q, R17_q, R18_q, R19_q, R20_q, R21_q, R22_q,
       R23_q, R24_q, R25_q, R26_q, R27_q, R28_q, R29_q, R30_q, R31_q, undriven, undriven_2, undriven_3,
       undriven_7, undriven_9, undriven_10, undriven_11, undriven_15, undriven_17, undriven_18, undriven_19,
       undriven_23, undriven_24, undriven_25, undriven_26, undriven_31, undriven_32, undriven_33,
       undriven_34, undriven_39, undriven_40, undriven_41, undriven_42, undriven_47, undriven_48,
       undriven_49, undriven_50, undriven_55, undriven_56, undriven_57, undriven_58;

  Register #(.width(32), .Select("low")) R8 (.D(undriven), .en(undriven_4), .Q(R8_q), .clk(Clock));  // open: clr
  Register #(.width(32), .Select("low")) R16 (.D(undriven_2), .en(undriven_5), .Q(R16_q), .clk(Clock));  // open: clr
  Register #(.width(32), .Select("low")) R24 (.D(undriven_3), .en(undriven_6), .Q(R24_q), .clk(Clock));  // open: clr
  Register #(.width(32), .Select("low")) R1 (.D(undriven_7), .en(undriven_8), .Q(R1_q), .clk(Clock));  // open: clr
  Register #(.width(32), .Select("low")) R9 (.D(undriven_9), .en(undriven_12), .Q(R9_q), .clk(Clock));  // open: clr
  Register #(.width(32), .Select("low")) R17 (.D(undriven_10), .en(undriven_13), .Q(R17_q), .clk(Clock));  // open: clr
  Register #(.width(32), .Select("low")) R25 (.D(undriven_11), .en(undriven_14), .Q(R25_q), .clk(Clock));  // open: clr
  Register #(.width(32), .Select("low")) R2 (.D(undriven_15), .en(undriven_16), .Q(R2_q), .clk(Clock));  // open: clr
  Register #(.width(32), .Select("low")) R10 (.D(undriven_17), .en(undriven_20), .Q(R10_q), .clk(Clock));  // open: clr
  Register #(.width(32), .Select("low")) R18 (.D(undriven_18), .en(undriven_21), .Q(R18_q), .clk(Clock));  // open: clr
  Register #(.width(32), .Select("low")) R26 (.D(undriven_19), .en(undriven_22), .Q(R26_q), .clk(Clock));  // open: clr
  Register #(.width(32), .Select("low")) R3 (.D(undriven_23), .en(undriven_27), .Q(R3_q), .clk(Clock));  // open: clr
  Register #(.width(32), .Select("low")) R11 (.D(undriven_24), .en(undriven_28), .Q(R11_q), .clk(Clock));  // open: clr
  Register #(.width(32), .Select("low")) R19 (.D(undriven_25), .en(undriven_29), .Q(R19_q), .clk(Clock));  // open: clr
  Register #(.width(32), .Select("low")) R27 (.D(undriven_26), .en(undriven_30), .Q(R27_q), .clk(Clock));  // open: clr
  Register #(.width(32), .Select("low")) R4 (.D(undriven_31), .en(undriven_35), .Q(R4_q), .clk(Clock));  // open: clr
  Register #(.width(32), .Select("low")) R5 (.D(undriven_39), .en(undriven_43), .Q(R5_q), .clk(Clock));  // open: clr
  Register #(.width(32), .Select("low")) R13 (.D(undriven_40), .en(undriven_44), .Q(R13_q), .clk(Clock));  // open: clr
  Register #(.width(32), .Select("low")) R12 (.D(undriven_32), .en(undriven_36), .Q(R12_q), .clk(Clock));  // open: clr
  Register #(.width(32), .Select("low")) R20 (.D(undriven_33), .en(undriven_37), .Q(R20_q), .clk(Clock));  // open: clr
  Register #(.width(32), .Select("low")) R21 (.D(undriven_41), .en(undriven_45), .Q(R21_q), .clk(Clock));  // open: clr
  Register #(.width(32), .Select("low")) R29 (.D(undriven_42), .en(undriven_46), .Q(R29_q), .clk(Clock));  // open: clr
  Register #(.width(32), .Select("low")) R28 (.D(undriven_34), .en(undriven_38), .Q(R28_q), .clk(Clock));  // open: clr
  Register #(.width(32), .Select("low")) R6 (.D(undriven_47), .en(undriven_51), .Q(R6_q), .clk(Clock));  // open: clr
  Register #(.width(32), .Select("low")) R14 (.D(undriven_48), .en(undriven_52), .Q(R14_q), .clk(Clock));  // open: clr
  Register #(.width(32), .Select("low")) R22 (.D(undriven_49), .en(undriven_53), .Q(R22_q), .clk(Clock));  // open: clr
  Register #(.width(32), .Select("low")) R30 (.D(undriven_50), .en(undriven_54), .Q(R30_q), .clk(Clock));  // open: clr
  Register #(.width(32), .Select("low")) R7 (.D(undriven_55), .en(undriven_59), .Q(R7_q), .clk(Clock));  // open: clr
  Register #(.width(32), .Select("low")) R15 (.D(undriven_56), .en(undriven_60), .Q(R15_q), .clk(Clock));  // open: clr
  Register #(.width(32), .Select("low")) R23 (.D(undriven_57), .en(undriven_61), .Q(R23_q), .clk(Clock));  // open: clr
  Register #(.width(32), .Select("low")) R31 (.D(undriven_58), .en(undriven_62), .Q(R31_q), .clk(Clock));  // open: clr
  Multiplexer #(.select(3), .width(32), .enable("false")) multiplexer_1 (
    .in0({32{1'b0}}), .in1(R1_q), .in2(R2_q), .in3(R3_q), .in4(R4_q), .in5(R5_q), .in6(R6_q), .in7(R7_q),
    .out(multiplexer_1_out), .sel(rs[2:0]));
  Multiplexer #(.select(3), .width(32), .enable("false")) multiplexer_2 (
    .in0({32{1'b0}}), .in1(R1_q), .in2(R2_q), .in3(R3_q), .in4(R4_q), .in5(R5_q), .in6(R6_q), .in7(R7_q),
    .out(multiplexer_2_out), .sel(rt[2:0]));
  Multiplexer #(.select(3), .width(32), .enable("false")) multiplexer_3 (
    .in0(R8_q), .in1(R9_q), .in2(R10_q), .in3(R11_q), .in4(R12_q), .in5(R13_q), .in6(R14_q), .in7(R15_q),
    .out(multiplexer_3_out), .sel(rs[2:0]));
  Multiplexer #(.select(3), .width(32), .enable("false")) multiplexer_4 (
    .in0(R8_q), .in1(R9_q), .in2(R10_q), .in3(R11_q), .in4(R12_q), .in5(R13_q), .in6(R14_q), .in7(R15_q),
    .out(multiplexer_4_out), .sel(rt[2:0]));
  Multiplexer #(.select(3), .width(32), .enable("false")) multiplexer_5 (
    .in0(R16_q), .in1(R17_q), .in2(R18_q), .in3(R19_q), .in4(R20_q), .in5(R21_q), .in6(R22_q), .in7(R23_q),
    .out(multiplexer_5_out), .sel(rs[2:0]));
  Multiplexer #(.select(3), .width(32), .enable("false")) multiplexer_6 (
    .in0(R16_q), .in1(R17_q), .in2(R18_q), .in3(R19_q), .in4(R20_q), .in5(R21_q), .in6(R22_q), .in7(R23_q),
    .out(multiplexer_6_out), .sel(rt[2:0]));
  Multiplexer #(.select(3), .width(32), .enable("false")) multiplexer_7 (
    .in0(R24_q), .in1(R25_q), .in2(R26_q), .in3(R27_q), .in4(R28_q), .in5(R29_q), .in6(R30_q), .in7(R31_q),
    .out(multiplexer_7_out), .sel(rs[2:0]));
  Multiplexer #(.select(3), .width(32), .enable("false")) multiplexer_8 (
    .in0(R24_q), .in1(R25_q), .in2(R26_q), .in3(R27_q), .in4(R28_q), .in5(R29_q), .in6(R30_q), .in7(R31_q),
    .out(multiplexer_8_out), .sel(rt[2:0]));

  // Other names for the same wires on the sheet: rd[4:0] = Write_register; rdl[2:0] = Write_register[2:0];
  //   rdh[1:0] = Write_register[4:3]; rsl[2:0] = rs[2:0]; rsh[1:0] = rs[4:3]; rtl[2:0] = rt[2:0]; rth[1:0] = rt[4:3]

  // Notes on the sheet:
  //   Entradas
  //   Control
  //   Salidas
endmodule
