// Logisim project alu.circ as structural Verilog
module ALU (
  input  Clock,
  input  [31:0] Operand_1,
  input  [31:0] Operand_2,
  input  [4:0] ShfAmt,
  input  [3:0] ALUOp,
  output [31:0] ALUResult,
  output Zero,
  output Less_than_zero,
  output Greater_than_zero
);

  wire comparator_1_lt;
  wire [31:0] adder_1_out, and_1_out, bit_extender_1_out, nor_1_out, or_1_out, shifter_1_out,
       subtractor_1_out, xor_1_out;

  Comparator #(.width(32)) comparator_1 (.a(Operand_1), .b(Operand_2), .lt(comparator_1_lt));  // open: gt, eq
  Shifter #(.width(32)) shifter_1 (.in(Operand_1), .\dist (ShfAmt), .out(shifter_1_out));
  Adder #(.width(32)) adder_1 (.a(Operand_1), .b(Operand_2), .out(adder_1_out));  // open: cin, cout
  Subtractor #(.width(32)) subtractor_1 (.a(Operand_1), .b(Operand_2), .out(subtractor_1_out));  // open: bin, bout
  assign and_1_out = Operand_1 & Operand_2;  // AND_Gate and_1, 32 bits wide
  assign or_1_out = Operand_1 | Operand_2;  // OR_Gate or_1, 32 bits wide
  assign xor_1_out = Operand_1 ^ Operand_2;  // XOR_Gate xor_1, 32 bits wide
  assign nor_1_out = ~(Operand_1 | Operand_2);  // NOR_Gate nor_1, 32 bits wide
  assign bit_extender_1_out = {{31{1'b0}}, comparator_1_lt};  // Bit_Extender bit_extender_1
  Comparator #(.width(32)) comparator_2 (
    .a(bit_extender_1_out), .b({32{1'b0}}), .gt(Less_than_zero), .eq(Zero), .lt(Greater_than_zero));
  Multiplexer #(.select(4), .width(32), .enable("false")) multiplexer_1 (
    .in0(adder_1_out), .in2(subtractor_1_out), .in4(and_1_out), .in5(or_1_out), .in6(xor_1_out),
    .in7(nor_1_out), .in10(bit_extender_1_out), .in12(shifter_1_out), .out(ALUResult), .sel(ALUOp));  // open: in1, in3, in8, in9, in11, in13, in14, in15

  // Notes on the sheet:
  //   Entradas
  //   Control
  //   Salidas
endmodule
